# Fritzing sketch LDR Synth (saved by Fritzing 0.9.3b)
circuit board: 15.0879cm x 11.2221cm

parts:
  U1 = LM 358 Dual Op-Amp [part_number=LM358 package="DIP8 [THT]"]
  U2 = LM 358 Dual Op-Amp [package="DIP8 [THT]"]
  U3 = LM 358 Dual Op-Amp [package="DIP8 [THT]"]
  U5 = LM 358 Dual Op-Amp [package="DIP8 [THT]"]
  S1 = Pushbutton [package="[THT]"]
  S2 = Pushbutton [package="[THT]"]
  S3 = Pushbutton [package="[THT]"]
  S4 = Pushbutton [package="[THT]"]
  S5 = Pushbutton [package="[THT]"]
  S6 = Pushbutton [package="[THT]"]
  S7 = Pushbutton [package="[THT]"]
  S8 = Pushbutton [package="[THT]"]
  R9 = Resistor [tolerance=±5% resistance=10k package=THT]
  R10 = Resistor [tolerance=±5% resistance=100k package=THT]
  R11 = Resistor [tolerance=±5% resistance=100k package=THT]
  R12 = Resistor [tolerance=±5% resistance=100k package=THT]
  R13 = Resistor [tolerance=±5% resistance=100k package=THT]
  R14 = Resistor [tolerance=±5% resistance=47k package=THT]
  R15 = Resistor [tolerance=±5% resistance=22k package=THT]
  R16 = Resistor [tolerance=±5% resistance=47k package=THT]
  C1 = Ceramic Capacitor [capacitance=0.22µF package="100 mil [THT, multilayer]"]
  R18 = Resistor [tolerance=±5% resistance=100k package=THT]
  R19 = Resistor [tolerance=±5% resistance=22k package=THT]
  R20 = Resistor [tolerance=±5% resistance=470k package=THT]
  C2 = Electrolytic Capacitor [capacitance=2.2µF package="100 mil [THT, electrolytic]"]
  R21 = Resistor [tolerance=±5% resistance=22k package=THT]
  R22 = Resistor [tolerance=±5% resistance=47k package=THT]
  R23 = Resistor [tolerance=±5% resistance=4.7k package=THT]
  C3 = Electrolytic Capacitor [capacitance=4.7µF package="100 mil [THT, electrolytic]"]
  R24 = Resistor [tolerance=±5% resistance=47k package=THT]
  R25 = Resistor [tolerance=±5% resistance=22k package=THT]
  Audio_Out = Loudspeaker
  C4 = Electrolytic Capacitor [capacitance=4.7µF package="100 mil [THT, electrolytic]"]
  R26 = Resistor [tolerance=±5% resistance=10k package=THT]
  R27 = Resistor [tolerance=±5% resistance=22k package=THT]
  C5 = Ceramic Capacitor [capacitance=10pF package="100 mil [THT, multilayer]"]
  R28 = Resistor [tolerance=±5% resistance=100k package=THT]
  R29 = Resistor [tolerance=±5% resistance=100k package=THT]
  LDR1 = Photocell (LDR) [package=THT]
  R31 = Resistor [tolerance=±5% resistance=10k package=THT]
  LDR2 = Photocell (LDR) [package=THT]
  C6 = Ceramic Capacitor [capacitance=10pF package="100 mil [THT, multilayer]"]
  R33 = Resistor [tolerance=±5% resistance=330k package=THT]
  U4 = LM 358 Dual Op-Amp [package="DIP8 [THT]"]
  9V = Power plug
  R1 = Trimmer Potentiometer [maximum_resistance=100kΩ package=THT]
  R7 = Trimmer Potentiometer [maximum_resistance=100kΩ package=THT]
  R8 = Trimmer Potentiometer [maximum_resistance=100kΩ package=THT]
  R6 = Trimmer Potentiometer [maximum_resistance=100kΩ package=THT]
  R5 = Trimmer Potentiometer [maximum_resistance=100kΩ package=THT]
  R4 = Trimmer Potentiometer [maximum_resistance=100kΩ package=THT]
  R3 = Trimmer Potentiometer [maximum_resistance=100kΩ package=THT]
  R2 = Trimmer Potentiometer [maximum_resistance=100kΩ package=THT]
  R17 = Rotary Potentiometer (Large) [maximum_resistance=100kΩ package=THT]
  Adjust_to_60k = Trimmer Potentiometer [maximum_resistance=100k package=THT]

nets:
  N1: U1.connector0, S1.Pin_1, S1.Pin_2, S2.Pin_1, S2.Pin_2, S3.Pin_1, S3.Pin_2, S4.Pin_1, S4.Pin_2, S5.Pin_1, S5.Pin_2, S6.Pin_1, S6.Pin_2, S7.Pin_1, S7.Pin_2, S8.Pin_2, R14.Pin_1
  N2: U1.connector1, U1.connector4, R10.Pin_0, R11.Pin_1
  N3: U1.connector2, R14.Pin_0, R15.Pin_0
  GND: U1.connector3, U2.connector3, U3.connector3, U5.connector3, R11.Pin_0, R12.Pin_0, R23.Pin_0, Audio_Out.pin2, R27.Pin_0, R28.Pin_0, U4.connector3, 9V.GND, R17.leg1
  N4: U1.connector5, R9.Pin_0, C1.1
  N5: U1.connector6, U3.connector1, R15.Pin_1, C1.0
  9V: U1.connector7, U2.connector7, U3.connector7, U5.connector7, R10.Pin_1, R13.Pin_1, R29.Pin_1, U4.connector7, 9V.VCC, R17.leg2
  N6: U2.connector0, R16.Pin_1, R20.Pin_1
  N7: U2.connector1, U2.connector4, R12.Pin_1, R13.Pin_0
  N8: U2.connector2, R16.Pin_0, R19.Pin_0
  N9: U2.connector5, R20.Pin_0, C2.-
  N10: U2.connector6, R18.Pin_0, R19.Pin_1, C2.+
  N11: U3.connector0, R22.Pin_1
  N12: U3.connector2, U3.connector6, R21.Pin_1
  N13: U3.connector4, R17.wiper
  N14: U3.connector5, R18.Pin_1, R21.Pin_0
  N15: U5.connector0, R26.Pin_1, C5.0
  N16: U5.connector1, C5.1, LDR2.pin_1
  N17: U5.connector2, R28.Pin_1, R29.Pin_0, U4.connector2
  N18: S1.Pin_3, S1.Pin_4, R1.wiper
  N19: S2.Pin_3, S2.Pin_4, R2.wiper
  N20: S3.Pin_3, S3.Pin_4, R3.wiper
  N21: S4.Pin_3, S4.Pin_4, R4.wiper
  N22: S5.Pin_3, S5.Pin_4, R5.wiper
  N23: S6.Pin_3, S6.Pin_4, R6.wiper
  N24: S7.Pin_3, S7.Pin_4, R7.wiper
  N25: S8.Pin_3, S8.Pin_4, R8.wiper
  N26: R9.Pin_1, R1.leg2, R7.leg2, R8.leg2, R6.leg2, R5.leg2, R4.leg2, R3.leg2, R2.leg2
  N27: R22.Pin_0, R23.Pin_1, C3.+
  N28: C3.-, R24.Pin_0
  N29: R24.Pin_1, R33.Pin_0, U4.connector4
  N30: R25.Pin_0, U4.connector5
  N31: R25.Pin_1, LDR1.pin_0, U4.connector6
  N32: Audio_Out.pin1, C4.-
  N33: C4.+, R26.Pin_0, R27.Pin_1
  N34: LDR1.pin_1, R31.Pin_0
  N35: R31.Pin_1, C6.1, U4.connector1
  N36: LDR2.pin_0, C6.0, U4.connector0, Adjust_to_60k.wiper
  N37: R33.Pin_1, Adjust_to_60k.leg2

notes:
  PWM Adjustment
